# Fritzing sketch Schéma du projet FINAL (saved by Fritzing 0.9.3b)
breadboards: 1

parts:
  Arduino_UNO = Arduino Uno (Rev3)
  R2 = Resistor [tolerance=±5% resistance=1M package=THT]
  R3 = Resistor [tolerance=±5% resistance=3.3k package=THT]
  L1 = Inductor [package="400 mil [THT]"]
  D1 = Rectifier Diode [part_number=1N4001 package="300 mil [THT]"]
  C1 = Ceramic Capacitor [capacitance=100nF package="100 mil [THT, multilayer]"]
  R1 = Resistor [tolerance=±5% resistance=10k package=THT]
  C2 = Ceramic Capacitor [capacitance=100nF package="100 mil [THT, multilayer]"]
  LED_activité = LED - 5mm [color="Red (633nm)" package="5 mm [THT]"]
  LED_2_doigts = LED - 5mm [color="Orange (620nm)" package="5 mm [THT]"]
  LED_1_doigt = LED - 5mm [color="Red (633nm)" package="5 mm [THT]"]
  LED_Grab = LED - 5mm [color="Green (560nm)" package="5 mm [THT]"]

nets:
  GND/patate avec électrode: Arduino_UNO.A0, Arduino_UNO.GND, R2.Pin_0, R2.Pin_1, R3.Pin_0, R3.Pin_1, L1.pin_0, L1.pin_1, D1.cathode, D1.anode, C1.0, C1.1, R1.Pin_0, C2.0, C2.1, LED_activité.cathode, LED_2_doigts.cathode, LED_1_doigt.cathode, LED_Grab.cathode
  N1: Arduino_UNO.D8, LED_activité.anode
  N2: Arduino_UNO.D9_PWM, R1.Pin_1
  N3: Arduino_UNO.D2, LED_1_doigt.anode
  N4: Arduino_UNO.D4, LED_2_doigts.anode
  N5: Arduino_UNO.D7, LED_Grab.anode
